# Fritzing sketch POC Wiring (saved by Fritzing 0.9.4)
circuit board: 8.46667cm x 5.64444cm
breadboards: 1

parts:
  U1 = LCD-16X2 [package=lcd-16x2]
  Composant1 = Arduino Uno (Rev3)

nets:
  N1: U1.R_W, Composant1.D10_PWM/SS, Composant1.D7
